// Logisim project gglu_v2.circ as structural Verilog: 1 circuit, main circuit main
module main (
  input  Clk,
  input  D,
  input  i1,
  input  i0,
  output Dbus,
  output RR,
  output W,
  output J
);

  wire and_1_out, multiplexer_2_out, nor_1_out, not_1_out, not_2_out;

  Multiplexer multiplexer_1 (.in0(D), .in1(RR), .out(Dbus), .sel(i1));
  nor nor_1 (nor_1_out, Dbus, RR);
  Multiplexer multiplexer_2 (.in0(Dbus), .in1(nor_1_out), .out(multiplexer_2_out), .sel(i0));
  and and_1 (and_1_out, Clk, not_1_out);
  not not_1 (not_1_out, i1);
  not not_2 (not_2_out, i0);
  D_Flip_Flop d_ff_1 (.D(multiplexer_2_out), .clk(and_1_out), .Q(RR));  // open: Qn, preset, reset
  and and_2 (W, i1, Clk, not_2_out);
  and and_3 (J, i1, Clk, i0, nor_1_out);

  // Other names for the same wires on the sheet: Clock = Clk; Data = D

  // Notes on the sheet:
  //   00: LD
  //   dbus = data
  //   write = 0
  //   jump = 0
  //   rr = dbus
  //   01: NOR
  //   dbus = data
  //   rr = !(rr + dbus)
  //   write = 0
  //   jump = 0
  //   10: STO
  //   write = 1
  //   jump = 0
  //   dbus = rr
  //   rr = rr
  //   11: JMP
  //   dbus = data
  //   rr = rr
  //   write = 0
  //   jump = 1
endmodule
